# Fritzing sketch Esquemático_DHT11 (saved by Fritzing 0.9.3b)

parts:
  M5Stack_Core = M5Stack Core (Back)
  DHT11 = KY-015 Temperature & Humidity Sensor Module [package="Breakout board"]

nets:
  N1: M5Stack_Core.Gnd, DHT11.-
  5V: M5Stack_Core.5V, DHT11.Vin
  N2: M5Stack_Core.5, DHT11.S

custom parts:
  M5Stack Core (Back): M5Stack ESP32 development kit
  KY-015 Temperature & Humidity Sensor Module: KY-015 temperature and humidity sensor module, provides a low-latency serial interface to measure humidity and temperature.
