# Fritzing sketch Esquemático_HX711 (saved by Fritzing 0.9.3b)

parts:
  Sensor_de_peso = Load Cell - Red/white/black/green
  part = HX711 Weighing Sensor Module
  M5Stack = M5Stack Core (Back)

nets:
  N1: Sensor_de_peso.wire1, part.E+
  N2: Sensor_de_peso.wire2, part.A+
  N3: Sensor_de_peso.wire3, part.E-
  N4: Sensor_de_peso.wire4, part.A-
  VCC: part.VCC, M5Stack.5V
  GND: part.GND, M5Stack.Gnd
  N5: part.DO/RX, M5Stack.18
  N6: part.CK/TX, M5Stack.19

custom parts:
  Load Cell - Red/white/black/green: A rectangle load cell/weighting pressure Sensor with four wires - Red, white, black, green. Normally corresponding with E+, E-, A+, A- respectively.
  HX711 Weighing Sensor Module: HX711 is a precision 24-bit analog-to-digital converter (ADC) designed for weigh scales and industrial control applications to interface directly with a bridge sensor.
  M5Stack Core (Back): M5Stack ESP32 development kit
